// Logisim project digilog5.circ as structural Verilog: 1 circuit, main circuit main
module main (
  input  a,
  input  b,
  input  c,
  input  d,
  input  in_5
);

  wire and_1_out, not_1_out, not_2_out, not_3_out, not_4_out, not_5_out, not_6_out, not_7_out, not_8_out,
       not_9_out, not_10_out, or_1_out, or_2_out, or_3_out, or_4_out, or_5_out, or_6_out;

  not not_1 (not_1_out, a);
  not not_2 (not_2_out, b);
  not not_3 (not_3_out, c);
  not not_4 (not_4_out, d);
  not not_5 (not_5_out, d);
  not not_6 (not_6_out, c);
  not not_7 (not_7_out, b);
  not not_8 (not_8_out, d);
  not not_9 (not_9_out, a);
  not not_10 (not_10_out, b);
  or or_1 (or_1_out, not_1_out, not_2_out, not_3_out, not_4_out);
  LED led_1 (.in(or_2_out));
  or or_2 (or_2_out, a, b, c, not_5_out);
  or or_3 (or_3_out, a, b, not_6_out, d);
  LED led_2 (.in(or_3_out));
  LED led_3 (.in(or_4_out));
  or or_4 (or_4_out, a, not_7_out, c, not_8_out);
  LED led_4 (.in(or_5_out));
  or or_5 (or_5_out, not_9_out, not_10_out, c, d);
  or or_6 (or_6_out, a, b, c, d);
  LED led_5 (.in(or_6_out));
  LED led_6 (.in(or_1_out));
  LED led_7 (.in(and_1_out));
  and and_1 (and_1_out, or_2_out, or_3_out, or_4_out, or_5_out, or_6_out, or_1_out);

  // Notes on the sheet:
  //   d
  //   a
  //   b
  //   c
  //   d
  //   a
  //   b
  //   c
  //   d
  //   a
  //   b
  //   c
  //   d
  //   a
  //   b
  //   c
  //   d
  //   a
  //   b
  //   c
  //   d
  //   a
  //   b
  //   c
endmodule
