// Logisim project digilogact3.circ as structural Verilog: 1 circuit, main circuit main
module main (
  input  y,
  input  z,
  input  in_3
);

  wire and_1_out, and_2_out, not_1_out, not_2_out, not_3_out, or_1_out;

  and and_1 (and_1_out, in_3, z, y);
  not not_1 (not_1_out, in_3);
  not not_2 (not_2_out, z);
  not not_3 (not_3_out, y);
  and and_2 (and_2_out, not_1_out, not_2_out, not_3_out);
  or or_1 (or_1_out, and_1_out, and_2_out);
  LED led_1 (.in(or_1_out));

  // Notes on the sheet:
  //   x
endmodule
