// Logisim project digilogexercise4.circ as structural Verilog: 1 circuit, main circuit main
module main (
  input  x,
  input  y,
  input  z
);

  wire and_1_out, and_2_out, and_3_out, and_4_out, and_5_out, not_1_out, not_2_out, not_3_out, not_4_out,
       not_5_out, not_6_out, or_1_out;

  not not_1 (not_1_out, x);
  not not_2 (not_2_out, y);
  not not_3 (not_3_out, z);
  not not_4 (not_4_out, y);
  not not_5 (not_5_out, z);
  not not_6 (not_6_out, x);
  and and_1 (and_1_out, x, y, z);
  and and_2 (and_2_out, not_1_out, not_2_out, z);
  and and_3 (and_3_out, x, y, not_3_out);
  and and_4 (and_4_out, x, not_4_out, not_5_out);
  and and_5 (and_5_out, not_6_out, y, z);
  LED led_1 (.in(or_1_out));
  or or_1 (or_1_out, and_1_out, and_2_out, and_3_out, and_4_out, and_5_out);

  // Notes on the sheet:
  //   x
  //   y
  //   x
  //   y
  //   x
  //   y
  //   x
  //   y
  //   x
  //   y
  //   z
  //   z
  //   z
  //   z
  //   z
endmodule
