// Logisim project ladsemifinalact1.circ as structural Verilog: 1 circuit, main circuit main
module main (
  input  x,
  input  z,
  input  y,
  output out_4,
  output out_5
);

  wire and_1_out, and_2_out, and_3_out, and_4_out, and_5_out, and_6_out, not_1_out, not_2_out, not_3_out,
       not_4_out, not_5_out, not_6_out, not_7_out, not_8_out, not_9_out, not_10_out, not_11_out, not_12_out,
       not_13_out, or_2_out, or_3_out, or_4_out;

  not not_1 (not_1_out, y);
  not not_2 (not_2_out, z);
  not not_3 (not_3_out, x);
  not not_4 (not_4_out, y);
  not not_5 (not_5_out, z);
  not not_6 (not_6_out, y);
  not not_7 (not_7_out, x);
  not not_8 (not_8_out, z);
  not not_9 (not_9_out, x);
  not not_10 (not_10_out, z);
  not not_11 (not_11_out, x);
  and and_1 (and_1_out, not_1_out, not_2_out, not_3_out);
  and and_2 (and_2_out, not_4_out, not_5_out, x);
  and and_3 (and_3_out, not_6_out, z, not_7_out);
  and and_4 (and_4_out, y, not_8_out, not_9_out);
  and and_5 (and_5_out, y, not_10_out, x);
  and and_6 (and_6_out, y, z, not_11_out);
  not not_12 (not_12_out, y);
  not not_13 (not_13_out, z);
  or or_1 (out_5, not_12_out, not_13_out);
  or or_2 (or_2_out, and_1_out, and_2_out);
  or or_3 (or_3_out, and_3_out, and_4_out);
  or or_4 (or_4_out, and_5_out, and_6_out);
  or or_5 (out_4, or_2_out, or_3_out, or_4_out);
endmodule
