// Logisim project midtermact3.circ as structural Verilog: 1 circuit, main circuit main
module main (
  input  b,
  input  c,
  input  in_3,
  input  a,
  input  c_2,
  input  c_3
);

  wire and_1_out, and_2_out, and_3_out, and_4_out, and_5_out, and_6_out, and_7_out, and_8_out, and_9_out,
       and_10_out, and_11_out, and_12_out, and_13_out, and_14_out, and_15_out, and_16_out, and_17_out,
       and_18_out, and_19_out, and_20_out, not_1_out, not_2_out, not_3_out, not_4_out, not_5_out, not_6_out,
       not_7_out, not_8_out, not_9_out, not_10_out, not_11_out, not_12_out, not_13_out, not_14_out,
       not_15_out, not_16_out, or_1_out, or_2_out, or_3_out, or_4_out, or_5_out, or_6_out;

  not not_1 (not_1_out, in_3);
  not not_2 (not_2_out, b);
  not not_3 (not_3_out, c);
  not not_4 (not_4_out, b);
  not not_5 (not_5_out, c);
  not not_6 (not_6_out, in_3);
  not not_7 (not_7_out, b);
  not not_8 (not_8_out, c);
  and and_1 (and_1_out, b, c, in_3);
  and and_2 (and_2_out, b, c, not_1_out);
  and and_3 (and_3_out, not_2_out, not_3_out, in_3);
  and and_4 (and_4_out, not_4_out, not_5_out, not_6_out);
  and and_5 (and_5_out, b, c);
  and and_6 (and_6_out, not_7_out, not_8_out);
  or or_1 (or_1_out, and_1_out, and_2_out, and_3_out, and_4_out);
  LED led_1 (.in(or_1_out));
  or or_2 (or_2_out, and_5_out, and_6_out);
  LED led_2 (.in(or_2_out));
  not not_9 (not_9_out, c_3);
  not not_10 (not_10_out, a);
  not not_11 (not_11_out, c_2);
  not not_12 (not_12_out, a);
  not not_13 (not_13_out, c_2);
  not not_14 (not_14_out, c_3);
  not not_15 (not_15_out, a);
  not not_16 (not_16_out, c_2);
  and and_7 (and_7_out, c_2, a);
  and and_8 (and_8_out, c_3, c_3);
  and and_9 (and_9_out, a, c_2);
  buf and_10 (and_10_out, not_9_out);  // AND_Gate
  and and_11 (and_11_out, not_10_out, not_11_out);
  buf and_12 (and_12_out, c_3);  // AND_Gate
  and and_13 (and_13_out, not_12_out, not_13_out);
  buf and_14 (and_14_out, not_14_out);  // AND_Gate
  and and_15 (and_15_out, c_2, a);
  and and_16 (and_16_out, not_15_out, not_16_out);
  and and_17 (and_17_out, and_7_out, and_8_out);
  and and_18 (and_18_out, and_9_out, and_10_out);
  and and_19 (and_19_out, and_11_out, and_12_out);
  and and_20 (and_20_out, and_13_out, and_14_out);
  or or_3 (or_3_out, and_15_out, and_16_out);
  LED led_3 (.in(or_3_out));
  or or_4 (or_4_out, and_19_out, and_20_out);
  or or_5 (or_5_out, and_17_out, and_18_out);
  LED led_4 (.in(or_6_out));
  or or_6 (or_6_out, or_5_out, or_4_out);

  // Notes on the sheet:
  //   a
  //   b
endmodule
