// Logisim project test12.circ as structural Verilog: 1 circuit, main circuit main
module main (
  input  a,
  input  b,
  input  c,
  input  d,
  input  e,
  input  f,
  input  a_2,
  input  b_2,
  output out_9,
  output out_10
);

  wire and_1_out, and_2_out, and_3_out, and_4_out, not_1_out, not_2_out, not_3_out, or_2_out;

  not not_1 (not_1_out, d);
  not not_2 (not_2_out, b_2);
  not not_3 (not_3_out, a_2);
  and and_1 (and_1_out, c, not_1_out);
  and and_2 (and_2_out, e, f);
  and and_3 (and_3_out, a_2, b_2);
  and and_4 (and_4_out, not_2_out, not_3_out);
  or or_1 (out_10, and_3_out, and_4_out);
  or or_2 (or_2_out, and_1_out, and_2_out);
  and and_5 (out_9, a, b, or_2_out);
endmodule
